# Fritzing sketch schematic (saved by Fritzing 0.7.12b)
breadboards: 1

parts:
  Arduino1 = Arduino
  R1 = Rotary Potentiometer (Small) [maximum_resistance=100kΩ]
  R2 = Rotary Potentiometer (Small) [maximum_resistance=100kΩ]

nets:
  N1: Arduino1.+5V, R1.leg2, R2.leg2
  N2: Arduino1.GND, R1.leg1, R2.leg1
  N3: Arduino1.A0, R2.wiper
  N4: Arduino1.A1, R1.wiper

notes:
  geekytheory.com
